# Fritzing sketch Light Relay (saved by Fritzing 0.9.3b)

parts:
  Raspberry_Pi_1 = Raspberry Pi 3 [part_number=RPI-3-V1.2]
  LED1 = LED - 5mm [color="Red (633nm)" package="5 mm [THT]"]
  U1 = BATTERY-2 [package=battery-aa]
  JP1 = Header 2 [package=screwterminal-3.5mm-2_lock]

nets:
  N1: Raspberry_Pi_1.GND, JP1.2
  N2: LED1.cathode, U1.-1
