# Fritzing sketch PIR (saved by Fritzing 0.9.3b)

parts:
  Raspberry_Pi_1 = Raspberry Pi 3 [part_number=RPI-3-V1.2]
  JP1 = Header 2 [package=screwterminal-3.5mm-2_lock]

nets:
  N1: Raspberry_Pi_1.GPIO6, JP1.2
